// Logisim project Demultiplexadores.circ as structural Verilog
module Demux_1_4_com_Portas (
  input  S1,
  input  S0,
  input  X,
  output Y0,
  output Y1,
  output Y2,
  output Y3
);

  wire not_1_out, not_2_out, not_3_out, not_4_out;

  not not_1 (not_1_out, S1);
  not not_2 (not_2_out, S0);
  not not_3 (not_3_out, S1);
  not not_4 (not_4_out, S0);
  and and_1 (Y3, S1, S0, X);
  and and_2 (Y0, not_1_out, not_2_out, X);
  and and_3 (Y1, not_3_out, S0, X);
  and and_4 (Y2, S1, not_4_out, X);
endmodule

module Demux_1_4 (
  input  X,
  input  [1:0] S1_S0,
  output Y0,
  output Y1,
  output Y2,
  output Y3
);

  Demultiplexer #(.select(2), .enable("false")) demultiplexer_1 (
    .out0(Y0), .out1(Y1), .out2(Y2), .out3(Y3), .in(X), .sel(S1_S0));
endmodule

module \Funções_Booleanas_com_DEMUX  (
  input  [1:0] A_B,
  input  [1:0] A_B_2,
  input  [2:0] A_B_C,
  output out_4,
  output f_A_B,
  output f_A_B_C
);

  wire demultiplexer_1_out0, demultiplexer_1_out3, demultiplexer_2_out0, demultiplexer_2_out1,
       demultiplexer_2_out3, demultiplexer_2_out5, demultiplexer_3_out0, demultiplexer_3_out1,
       demultiplexer_3_out3;

  Demultiplexer #(.select(2), .enable("false")) demultiplexer_1 (
    .out0(demultiplexer_1_out0), .out3(demultiplexer_1_out3), .in(1'b1), .sel(A_B));  // open: out1, out2
  Demultiplexer #(.select(3), .enable("false")) demultiplexer_2 (
    .out0(demultiplexer_2_out0), .out1(demultiplexer_2_out1), .out3(demultiplexer_2_out3),
    .out5(demultiplexer_2_out5), .in(1'b1), .sel(A_B_C));  // open: out2, out4, out6, out7
  or or_1 (f_A_B, demultiplexer_1_out0, demultiplexer_1_out3);
  or or_2 (f_A_B_C, demultiplexer_2_out0, demultiplexer_2_out1, demultiplexer_2_out3, demultiplexer_2_out5);
  Demultiplexer #(.select(2), .enable("false")) demultiplexer_3 (
    .out0(demultiplexer_3_out0), .out1(demultiplexer_3_out1), .out3(demultiplexer_3_out3), .in(1'b1),
    .sel(A_B_2));  // open: out2
  or or_3 (out_4, demultiplexer_3_out0, demultiplexer_3_out1, demultiplexer_3_out3);

  // Notes on the sheet:
  //   f(A,B) = m0+m3 = ~A~B + AB
  //   DEMUX 1:4
  //   DEMUX 1:8
  //   f(A,B,C) = m0+m1+m3+m5 = Y0+Y1+Y3+Y5 = ~A~B~C + ~A~B C + ~ABC + A~BC
  //   DEMUX 1:4
  //   f(A,B) = m0+m1+m3= Y0+Y1+Y3 = ~A~B + A~B + AB
endmodule

module \Associação_em_Série  (
  input  X,
  input  [1:0] A_B,
  input  [1:0] C_D,
  output Y0,
  output Y1,
  output Y2,
  output Y3,
  output Y4,
  output Y5,
  output Y6,
  output Y7,
  output Y8,
  output Y9,
  output Y10,
  output Y11,
  output Y12,
  output Y13,
  output Y14,
  output Y15
);

  wire demultiplexer_1_out0, demultiplexer_1_out1, demultiplexer_1_out2, demultiplexer_1_out3;

  Demultiplexer #(.select(2), .enable("false")) demultiplexer_1 (
    .out0(demultiplexer_1_out0), .out1(demultiplexer_1_out1), .out2(demultiplexer_1_out2),
    .out3(demultiplexer_1_out3), .in(X), .sel(A_B));
  Demultiplexer #(.select(2), .enable("false")) demultiplexer_2 (
    .out0(Y0), .out1(Y1), .out2(Y2), .out3(Y3), .in(demultiplexer_1_out0), .sel(C_D));
  Demultiplexer #(.select(2), .enable("false")) demultiplexer_3 (
    .out0(Y4), .out1(Y5), .out2(Y6), .out3(Y7), .in(demultiplexer_1_out1), .sel(C_D));
  Demultiplexer #(.select(2), .enable("false")) demultiplexer_4 (
    .out0(Y8), .out1(Y9), .out2(Y10), .out3(Y11), .in(demultiplexer_1_out2), .sel(C_D));
  Demultiplexer #(.select(2), .enable("false")) demultiplexer_5 (
    .out0(Y12), .out1(Y13), .out2(Y14), .out3(Y15), .in(demultiplexer_1_out3), .sel(C_D));

  // Notes on the sheet:
  //   ASSOCIAÇÃO EM SÉRIE
endmodule

module \Associação_em_Paralelo  (
  input  X0,
  input  X1,
  input  X2,
  input  X3,
  input  [1:0] A_B,
  output Y0,
  output Y1,
  output Y2,
  output Y3,
  output Y4,
  output Y5,
  output Y6,
  output Y7,
  output Y8,
  output Y9,
  output Y10,
  output Y11,
  output Y12,
  output Y13,
  output Y14,
  output Y15
);

  Demultiplexer #(.select(2), .enable("false")) demultiplexer_1 (
    .out0(Y0), .out1(Y1), .out2(Y2), .out3(Y3), .in(X0), .sel(A_B));
  Demultiplexer #(.select(2), .enable("false")) demultiplexer_2 (
    .out0(Y4), .out1(Y5), .out2(Y6), .out3(Y7), .in(X1), .sel(A_B));
  Demultiplexer #(.select(2), .enable("false")) demultiplexer_3 (
    .out0(Y8), .out1(Y9), .out2(Y10), .out3(Y11), .in(X2), .sel(A_B));
  Demultiplexer #(.select(2), .enable("false")) demultiplexer_4 (
    .out0(Y12), .out1(Y13), .out2(Y14), .out3(Y15), .in(X3), .sel(A_B));

  // Notes on the sheet:
  //   ASSOCIAÇÃO EM PARALELO
endmodule
