// Logisim project Multiplexadores.circ as structural Verilog
module MUX_2_1 (
  input  S0,
  input  [1:0] X1_X0,
  input  [1:0] X1_X0_2,
  input  S0_2,
  output Y,
  output Y_2
);

  wire and_1_out, and_2_out, not_1_out;

  not not_1 (not_1_out, S0);
  Multiplexer #(.enable("false")) multiplexer_1 (.in0(X1_X0_2[0]), .in1(X1_X0_2[1]), .out(Y_2), .sel(S0_2));
  and and_1 (and_1_out, not_1_out, X1_X0[0]);
  and and_2 (and_2_out, S0, X1_X0[1]);
  or or_1 (Y, and_1_out, and_2_out);

  // Notes on the sheet:
  //   MUX 2:1
  //   Y = ~S0 X0 + S0 X1
endmodule

module MUX_4_1 (
  input  [3:0] X3_X2_X1_X0,
  input  [1:0] S1_S0,
  output out_3
);

  Multiplexer #(.select(2), .disabled(0), .enable("false")) multiplexer_1 (
    .in0(X3_X2_X1_X0[0]), .in1(X3_X2_X1_X0[1]), .in2(X3_X2_X1_X0[2]), .in3(X3_X2_X1_X0[3]), .out(out_3),
    .sel(S1_S0));

  // Notes on the sheet:
  //   MUX 4:1
  //   Y = ~S1~S0X0 + ~S1S0X1 + S1~S0X2 + S1S0X3 
endmodule

module MUX_em_Cascata (
  input  [3:0] X3_X2_X1_X0,
  input  [1:0] S1_S0,
  output Y
);

  wire multiplexer_1_out, multiplexer_2_out;

  Multiplexer #(.disabled(0), .enable("false")) multiplexer_1 (
    .in0(X3_X2_X1_X0[0]), .in1(X3_X2_X1_X0[1]), .out(multiplexer_1_out), .sel(S1_S0[0]));
  Multiplexer #(.disabled(0), .enable("false")) multiplexer_2 (
    .in0(X3_X2_X1_X0[2]), .in1(X3_X2_X1_X0[3]), .out(multiplexer_2_out), .sel(S1_S0[0]));
  Multiplexer #(.disabled(0), .enable("false")) multiplexer_3 (
    .in0(multiplexer_1_out), .in1(multiplexer_2_out), .out(Y), .sel(S1_S0[1]));

  // Notes on the sheet:
  //   MUX 4:1
  //   (MUXes 2:1 EM CASCATA)
endmodule

module \Função_Booleana_com_MUX  (
  input  A,
  input  C,
  input  B,
  input  D,
  input  C_2,
  input  D_2,
  input  [1:0] A_B,
  input  D_3,
  input  [2:0] A_B_C,
  input  [3:0] A_B_C_D,
  output Y,
  output Y_2,
  output Y_3,
  output Y_4
);

  wire and_1_out, and_2_out, and_3_out, and_4_out, and_5_out, and_6_out, nor_1_out, not_1_out, not_2_out,
       not_3_out, not_4_out, not_5_out, not_6_out, not_7_out, not_8_out, not_9_out, not_10_out, not_11_out,
       not_12_out, xor_1_out;

  not not_1 (not_1_out, A);
  not not_2 (not_2_out, B);
  not not_3 (not_3_out, C_2);
  not not_4 (not_4_out, D_2);
  not not_5 (not_5_out, A);
  not not_6 (not_6_out, C_2);
  not not_7 (not_7_out, A);
  not not_8 (not_8_out, D_2);
  not not_9 (not_9_out, B);
  not not_10 (not_10_out, C_2);
  not not_11 (not_11_out, D_2);
  and and_1 (and_1_out, not_1_out, not_2_out, not_3_out, not_4_out);
  and and_2 (and_2_out, not_5_out, B, not_6_out, D_2);
  and and_3 (and_3_out, not_7_out, B, C_2, not_8_out);
  and and_4 (and_4_out, A, not_9_out, not_10_out, not_11_out);
  and and_5 (and_5_out, A, B, C_2, D_2);
  Multiplexer #(.select(4), .disabled(0), .enable("false")) multiplexer_1 (
    .in0(1'b1), .in1(1'b0), .in2(1'b0), .in3(1'b0), .in4(1'b0), .in5(1'b1), .in6(1'b1), .in7(1'b0),
    .in8(1'b1), .in9(1'b0), .in10(1'b0), .in11(1'b0), .in12(1'b0), .in13(1'b0), .in14(1'b0), .in15(1'b1),
    .out(Y_4), .sel(A_B_C_D));
  or or_1 (Y_2, and_1_out, and_2_out, and_3_out, and_4_out, and_5_out);
  not not_12 (not_12_out, D_3);
  nor nor_1 (nor_1_out, C, D);
  xor xor_1 (xor_1_out, C, D);
  and and_6 (and_6_out, C, D);
  Multiplexer #(.select(2), .disabled(0), .enable("false")) multiplexer_2 (
    .in0(nor_1_out), .in1(xor_1_out), .in2(nor_1_out), .in3(and_6_out), .out(Y), .sel(A_B));
  Multiplexer #(.select(3), .disabled(0), .enable("false")) multiplexer_3 (
    .in0(not_12_out), .in1(1'b0), .in2(D_3), .in3(not_12_out), .in4(not_12_out), .in5(1'b0), .in6(1'b0),
    .in7(D_3), .out(Y_3), .sel(A_B_C));

  // Notes on the sheet:
  //   Y_3: pull=up
  //   f(A,B,C,D) = ~A~B~C~D + ~A B ~C D + ~A B C ~D + A ~B~C~D + A B C D 
  //   Função Booleana Implementada com MUX
endmodule

module \Função_Booleana_de_7_Variávies  (
  input  [2:0] A_B_C,
  input  [3:0] D_E_F_G,
  output f_A_B_C_D_E_F_G
);

  wire multiplexer_1_out, multiplexer_2_out, multiplexer_3_out, multiplexer_4_out, multiplexer_5_out;

  Multiplexer #(.select(4), .enable("false")) multiplexer_1 (
    .in0(1'b0), .in1(1'b0), .in2(1'b0), .in3(1'b1), .in4(1'b0), .in5(1'b0), .in6(1'b0), .in7(1'b0),
    .in8(1'b0), .in9(1'b0), .in10(1'b0), .in11(1'b0), .in12(1'b0), .in13(1'b0), .in14(1'b0), .in15(1'b0),
    .out(multiplexer_1_out), .sel(D_E_F_G));
  Multiplexer #(.select(4), .enable("false")) multiplexer_2 (
    .in0(1'b0), .in1(1'b0), .in2(1'b0), .in3(1'b0), .in4(1'b0), .in5(1'b0), .in6(1'b0), .in7(1'b0),
    .in8(1'b0), .in9(1'b0), .in10(1'b0), .in11(1'b0), .in12(1'b0), .in13(1'b0), .in14(1'b1), .in15(1'b0),
    .out(multiplexer_2_out), .sel(D_E_F_G));
  Multiplexer #(.select(4), .enable("false")) multiplexer_3 (
    .in0(1'b0), .in1(1'b0), .in2(1'b0), .in3(1'b0), .in4(1'b0), .in5(1'b0), .in6(1'b0), .in7(1'b1),
    .in8(1'b0), .in9(1'b1), .in10(1'b0), .in11(1'b0), .in12(1'b0), .in13(1'b0), .in14(1'b0), .in15(1'b0),
    .out(multiplexer_3_out), .sel(D_E_F_G));
  Multiplexer #(.select(4), .enable("false")) multiplexer_4 (
    .in0(1'b0), .in1(1'b0), .in2(1'b0), .in3(1'b0), .in4(1'b0), .in5(1'b1), .in6(1'b0), .in7(1'b1),
    .in8(1'b0), .in9(1'b0), .in10(1'b0), .in11(1'b0), .in12(1'b0), .in13(1'b0), .in14(1'b0), .in15(1'b0),
    .out(multiplexer_4_out), .sel(D_E_F_G));
  Multiplexer #(.select(4), .enable("false")) multiplexer_5 (
    .in0(1'b1), .in1(1'b1), .in2(1'b0), .in3(1'b0), .in4(1'b0), .in5(1'b0), .in6(1'b0), .in7(1'b0),
    .in8(1'b0), .in9(1'b0), .in10(1'b0), .in11(1'b0), .in12(1'b0), .in13(1'b0), .in14(1'b0), .in15(1'b0),
    .out(multiplexer_5_out), .sel(D_E_F_G));
  Multiplexer #(.select(3), .enable("false")) multiplexer_6 (
    .in0(1'b0), .in1(multiplexer_1_out), .in2(multiplexer_2_out), .in3(1'b0), .in4(multiplexer_3_out),
    .in5(1'b1), .in6(multiplexer_4_out), .in7(multiplexer_5_out), .out(f_A_B_C_D_E_F_G), .sel(A_B_C));

  // Notes on the sheet:
  //   MUX 16:1
  //   Y1
  //   Y2
  //   Y4
  //   Y6
  //   Y7
  //   f(A,B,C,D,E,F,G) = ~A~BC~D~EFG + ~AB~CDEF~G + A~B~CD~E~FG + A~B~C~DEFG + A~BC + AB~C~DEG + ABC~D~E~F
  //   MUX 8:1
endmodule

module \_7_Variáveis_com_Portas  (
  input  A,
  input  B,
  input  C,
  input  D,
  input  E,
  input  F,
  input  G,
  output Y
);

  wire and_1_out, and_2_out, and_3_out, and_4_out, and_5_out, and_6_out, and_7_out, not_1_out, not_2_out,
       not_3_out, not_4_out, not_5_out, not_6_out, not_7_out, not_8_out, not_9_out, not_10_out, not_11_out,
       not_12_out, not_13_out, not_14_out, not_15_out, not_16_out, not_17_out, not_18_out, not_19_out,
       not_20_out;

  not not_1 (not_1_out, A);
  not not_2 (not_2_out, B);
  not not_3 (not_3_out, D);
  not not_4 (not_4_out, E);
  not not_5 (not_5_out, A);
  not not_6 (not_6_out, C);
  not not_7 (not_7_out, G);
  not not_8 (not_8_out, B);
  not not_9 (not_9_out, C);
  not not_10 (not_10_out, E);
  not not_11 (not_11_out, F);
  not not_12 (not_12_out, B);
  not not_13 (not_13_out, C);
  not not_14 (not_14_out, D);
  not not_15 (not_15_out, C);
  not not_16 (not_16_out, D);
  not not_17 (not_17_out, D);
  not not_18 (not_18_out, E);
  not not_19 (not_19_out, F);
  and and_1 (and_1_out, not_1_out, not_2_out, C, not_3_out, not_4_out, F, G);
  and and_2 (and_2_out, not_5_out, B, not_6_out, D, E, F, not_7_out);
  and and_3 (and_3_out, A, not_8_out, not_9_out, D, not_10_out, not_11_out, G);
  and and_4 (and_4_out, A, not_12_out, not_13_out, not_14_out, E, F, G);
  and and_5 (and_5_out, A, not_20_out, C);
  not not_20 (not_20_out, B);
  and and_6 (and_6_out, A, B, not_15_out, not_16_out, E, G);
  and and_7 (and_7_out, A, B, C, not_17_out, not_18_out, not_19_out);
  or or_1 (Y, and_1_out, and_2_out, and_3_out, and_4_out, and_5_out, and_6_out, and_7_out);
endmodule

module \Função_Booleana_AB_CD  (
  input  [2:0] A_B_C,
  input  D,
  input  [3:0] A_B_C_D,
  input  A,
  input  B,
  input  [1:0] C_D,
  input  [1:0] A_B,
  input  [1:0] C_D_2,
  output out_9,
  output out_10,
  output out_11,
  output out_12
);

  wire and_1_out, and_2_out;

  Multiplexer #(.select(4), .enable("false")) multiplexer_1 (
    .in0(1'b0), .in1(1'b0), .in2(1'b0), .in3(1'b1), .in4(1'b0), .in5(1'b0), .in6(1'b0), .in7(1'b1),
    .in8(1'b0), .in9(1'b0), .in10(1'b0), .in11(1'b1), .in12(1'b1), .in13(1'b1), .in14(1'b1), .in15(1'b1),
    .out(out_10), .sel(A_B_C_D));
  and and_1 (and_1_out, C_D_2[0], C_D_2[1]);
  Multiplexer #(.select(2), .enable("false")) multiplexer_2 (
    .in0(and_1_out), .in1(and_1_out), .in2(and_1_out), .in3(1'b1), .out(out_12), .sel(A_B));
  and and_2 (and_2_out, C_D[0], C_D[1]);
  Multiplexer #(.select(3), .enable("false")) multiplexer_3 (
    .in0(1'b0), .in1(D), .in2(1'b0), .in3(D), .in4(1'b0), .in5(D), .in6(1'b1), .in7(1'b1), .out(out_9),
    .sel(A_B_C));
  Multiplexer #(.enable("false")) multiplexer_4 (.in0(and_2_out), .in1(B), .out(out_11), .sel(A));

  // Notes on the sheet:
  //   MUX 16:1
  //   MUX 4:1
  //   f(A,B,C,D) = A B + C D
  //   MUX 8:1
  //   MUX 2:1
endmodule

module \Associação_em_Paralelo  (
  input  [3:0] X0_X1_X2_X3,
  input  [3:0] X4_X5_X6_X7,
  input  [3:0] X8_X9_X10_X11,
  input  [3:0] X12_X13_X14_X15,
  input  [1:0] A_B,
  output X0__X3,
  output X4__X7,
  output X8__X11,
  output X12__X15
);

  Multiplexer #(.select(2), .enable("false")) multiplexer_1 (
    .in0(X0_X1_X2_X3[0]), .in1(X0_X1_X2_X3[1]), .in2(X0_X1_X2_X3[2]), .in3(X0_X1_X2_X3[3]), .out(X0__X3),
    .sel(A_B));
  Multiplexer #(.select(2), .enable("false")) multiplexer_2 (
    .in0(X4_X5_X6_X7[0]), .in1(X4_X5_X6_X7[1]), .in2(X4_X5_X6_X7[2]), .in3(X4_X5_X6_X7[3]), .out(X4__X7),
    .sel(A_B));
  Multiplexer #(.select(2), .enable("false")) multiplexer_3 (
    .in0(X8_X9_X10_X11[0]), .in1(X8_X9_X10_X11[1]), .in2(X8_X9_X10_X11[2]), .in3(X8_X9_X10_X11[3]),
    .out(X8__X11), .sel(A_B));
  Multiplexer #(.select(2), .enable("false")) multiplexer_4 (
    .in0(X12_X13_X14_X15[0]), .in1(X12_X13_X14_X15[1]), .in2(X12_X13_X14_X15[2]), .in3(X12_X13_X14_X15[3]),
    .out(X12__X15), .sel(A_B));

  // Notes on the sheet:
  //   ASSOCIAÇÃO EM PARALELO
endmodule

module \Associação_em_Série  (
  input  [3:0] X0_X1_X2_X3,
  input  [3:0] X4_X5_X6_X7,
  input  [3:0] X8_X9_X10_X11,
  input  [3:0] X12_X13_X14_X15,
  input  [1:0] C_D,
  input  [1:0] A_B,
  output Y
);

  wire multiplexer_1_out, multiplexer_2_out, multiplexer_3_out, multiplexer_4_out;

  Multiplexer #(.select(2), .enable("false")) multiplexer_1 (
    .in0(X0_X1_X2_X3[0]), .in1(X0_X1_X2_X3[1]), .in2(X0_X1_X2_X3[2]), .in3(X0_X1_X2_X3[3]),
    .out(multiplexer_1_out), .sel(C_D));
  Multiplexer #(.select(2), .enable("false")) multiplexer_2 (
    .in0(X4_X5_X6_X7[0]), .in1(X4_X5_X6_X7[1]), .in2(X4_X5_X6_X7[2]), .in3(X4_X5_X6_X7[3]),
    .out(multiplexer_2_out), .sel(C_D));
  Multiplexer #(.select(2), .enable("false")) multiplexer_3 (
    .in0(X8_X9_X10_X11[0]), .in1(X8_X9_X10_X11[1]), .in2(X8_X9_X10_X11[2]), .in3(X8_X9_X10_X11[3]),
    .out(multiplexer_3_out), .sel(C_D));
  Multiplexer #(.select(2), .enable("false")) multiplexer_4 (
    .in0(X12_X13_X14_X15[0]), .in1(X12_X13_X14_X15[1]), .in2(X12_X13_X14_X15[2]), .in3(X12_X13_X14_X15[3]),
    .out(multiplexer_4_out), .sel(C_D));
  Multiplexer #(.select(2), .enable("false")) multiplexer_5 (
    .in0(multiplexer_1_out), .in1(multiplexer_2_out), .in2(multiplexer_3_out), .in3(multiplexer_4_out),
    .out(Y), .sel(A_B));

  // Notes on the sheet:
  //   ASSOCIAÇÃO EM SÉRIE
  //   (LSB)
  //   (MSB)
endmodule
