// Logisim project Somadores.circ as structural Verilog: 3 circuits, main circuit SomadorCascata
module MeioSomador (
  input  A,
  input  B,
  output Soma,
  output Cout
);

  wire nand_1_out, nand_2_out, nand_3_out, nand_4_out, nand_5_out;

  nand nand_1 (nand_1_out, A, A);
  nand nand_2 (nand_2_out, B, B);
  nand nand_3 (nand_3_out, A, B);
  nand nand_4 (nand_4_out, nand_1_out, B);
  nand nand_5 (nand_5_out, A, nand_2_out);
  nand nand_6 (Cout, nand_3_out, nand_3_out);
  nand nand_7 (Soma, nand_4_out, nand_5_out);

  // Notes on the sheet:
  //   Meio Somador (1 bit)
endmodule

module SomadorCompleto (
  input  A,
  input  B,
  input  Cin,
  output Soma,
  output Cout
);

  wire and_1_out, and_2_out, xor_1_out;

  xor xor_1 (xor_1_out, A, B);
  xor xor_2 (Soma, xor_1_out, Cin);
  and and_1 (and_1_out, xor_1_out, Cin);
  and and_2 (and_2_out, A, B);
  or or_1 (Cout, and_1_out, and_2_out);

  // Notes on the sheet:
  //   Somador Completo (c/ portas)
endmodule

module SomadorCascata (
  input  B3,
  input  B2,
  input  B1,
  input  B0,
  input  A3,
  input  A2,
  input  A1,
  input  A0,
  output S3,
  output S2,
  output S1,
  output S0
);

  wire adder_1_cout, adder_2_cout, adder_3_cout, adder_4_cout;

  LED led_1 (.in(adder_1_cout));
  Adder #(.width(1)) adder_1 (.a(B3), .b(A3), .out(S3), .cin(adder_2_cout), .cout(adder_1_cout));
  Adder #(.width(1)) adder_2 (.a(B2), .b(A2), .out(S2), .cin(adder_3_cout), .cout(adder_2_cout));
  Adder #(.width(1)) adder_3 (.a(B1), .b(A1), .out(S1), .cin(adder_4_cout), .cout(adder_3_cout));
  Adder #(.width(1)) adder_4 (.a(B0), .b(A0), .out(S0), .cin(1'b0), .cout(adder_4_cout));

  // Notes on the sheet:
  //   Somador Completo (4 bits)
endmodule
